# Fritzing sketch Sketch (saved by Fritzing 0.9.7b)
breadboards: 1

parts:
  U1 = ESP8266 WiFi Module [part_number=ESP8266]
  Switch = SWITCH-SPST-2 [package=r_sw_th]
  Factory_Reset_Button = SWITCH-MOMENTARY-2 [package=tactile_switch_tall]

nets:
  N1: U1.RXD, Switch.P
  N2: U1.GND, Switch.O, Factory_Reset_Button.1
  N3: U1.TXD, Factory_Reset_Button.2

custom parts:
  ESP8266 WiFi Module: Generic WiFi Module based on the ESP8266 with onboard PCB antenna and UART communications
